# Fritzing sketch modbus_files (saved by Fritzing 0.9.3b)

parts:
  U2 = ESP8266 NodeMCU LoLin module
  U3 = RS485 [package=so08]
  U5 = RS485 [package=so08]
  U6 = RS485 [package=so08]
  U7 = RS485 [package=so08]
  U8 = RS485 [package=so08]

nets:
  N1: U2.D0, U3.EN
  N2: U2.D1, U3.TXD
  N3: U2.D2, U3.RXD
  3V3: U2.3V3, U3.VCC
  GND: U2.GND, U3.GND
  N4: U3.A, U5.A+
  N5: U3.B, U5.B-
  N6: U5.IN1, U6.OUT
  N7: U5.GND#2, U6.GND#0
  N8: U7.OUT, U8.IN1

notes:
  +12V
  GND
  +VAR

custom parts:
  ESP8266 NodeMCU LoLin module: ESP8266 based NodeMCU
  RS485: RS485 transceiver
  RS485: RS485 transceiver
  RS485: RS485 transceiver
  RS485: RS485 transceiver
